// Logisim project e2309953.circ as structural Verilog: 1 circuit, main circuit main
module main (
  input  A1,
  input  A0,
  input  B1,
  input  B0,
  input  S0,
  input  S1,
  output X2,
  output X1,
  output X0,
  output Y7,
  output Y6,
  output Y5,
  output Y4,
  output Y3,
  output Y2,
  output Y1,
  output Y0
);

  wire and_1_out, and_2_out, and_3_out, and_4_out, and_5_out, and_6_out, and_7_out, and_8_out, and_9_out,
       and_10_out, and_11_out, and_12_out, n3_to_8_decoder_74138_1_p3, n3_to_8_decoder_74138_1_p5,
       n3_to_8_decoder_74138_1_p7, n3_to_8_decoder_74138_1_p8, n3_to_8_decoder_74138_1_p9,
       n3_to_8_decoder_74138_1_p10, n3_to_8_decoder_74138_1_p11, n3_to_8_decoder_74138_1_p13,
       n3_to_8_decoder_74138_2_p2, n3_to_8_decoder_74138_2_p4, n3_to_8_decoder_74138_2_p6,
       n3_to_8_decoder_74138_2_p7, n3_to_8_decoder_74138_2_p8, n3_to_8_decoder_74138_2_p9,
       n3_to_8_decoder_74138_2_p10, n3_to_8_decoder_74138_2_p11, n3_to_8_decoder_74138_2_p13, not_1_out,
       not_3_out, not_4_out, not_5_out, not_6_out, or_1_out, or_2_out, or_3_out, or_4_out, or_5_out,
       or_6_out, or_7_out, or_8_out, xor_1_out, xor_2_out;

  or or_1 (or_1_out, B0, n3_to_8_decoder_74138_1_p3);
  not not_1 (not_1_out, B0);
  // _3_to_8_decoder__74138 #(.Facing("south")) 3_to_8_decoder_74138_1: pin names not known; wires that end beside it: not_1_out, B1, n3_to_8_decoder_74138_1_p3, A0, n3_to_8_decoder_74138_1_p5, A1, n3_to_8_decoder_74138_1_p7, n3_to_8_decoder_74138_1_p8, n3_to_8_decoder_74138_1_p9, n3_to_8_decoder_74138_1_p10, n3_to_8_decoder_74138_1_p11, 1'b1, n3_to_8_decoder_74138_1_p13, n3_to_8_decoder_74138_1_p13
  or or_2 (or_2_out, B0, n3_to_8_decoder_74138_1_p9);
  and and_1 (and_1_out, or_1_out, or_2_out);
  and and_2 (and_2_out, and_1_out, n3_to_8_decoder_74138_1_p7);
  and and_3 (and_3_out, and_2_out, n3_to_8_decoder_74138_1_p11);
  not not_2 (n3_to_8_decoder_74138_1_p13, 1'b1);
  and and_4 (and_4_out, n3_to_8_decoder_74138_1_p8, and_3_out);
  xor xor_1 (xor_1_out, B0, A0);
  or or_3 (or_3_out, n3_to_8_decoder_74138_1_p8, not_1_out);
  or or_4 (or_4_out, n3_to_8_decoder_74138_1_p5, not_1_out);
  and and_5 (and_5_out, or_4_out, or_3_out);
  and and_6 (and_6_out, n3_to_8_decoder_74138_1_p10, and_4_out);
  xor xor_2 (xor_2_out, B1, A1);
  not not_3 (not_3_out, xor_2_out);
  and and_7 (and_7_out, and_5_out, and_3_out);
  and and_8 (and_8_out, B1, B0);
  and and_9 (and_9_out, B1, A1);
  or or_5 (or_5_out, and_9_out, xor_2_out);
  not not_4 (not_4_out, 1'b1);
  and and_10 (and_10_out, xor_2_out, or_6_out);
  and and_11 (and_11_out, A1, A0);
  or or_6 (or_6_out, and_8_out, and_11_out);
  and and_12 (and_12_out, or_7_out, not_3_out);
  not not_5 (not_5_out, 1'b1);
  or or_7 (or_7_out, A0, B0);
  or or_8 (or_8_out, and_12_out, and_10_out);
  not not_6 (not_6_out, 1'b1);
  // _4_to_1_MUX__x2___74153 #(.Facing("east")) 4_to_1_mux_x2_74153_1: pin names not known; wires that end beside it: and_6_out, not_4_out, B1, A1, and_7_out, or_5_out, B0, not_6_out, not_6_out, not_1_out, X2, X1, A1, A0, B1, B0
  // _4_to_1_MUX__x2___74153 #(.Facing("east")) 4_to_1_mux_x2_74153_2: pin names not known; wires that end beside it: A0, xor_1_out, or_8_out, not_5_out, 1'b1, S0, not_6_out, S0, S1, not_6_out, S1, X0
  // _3_to_8_decoder__74138 #(.Facing("south")) 3_to_8_decoder_74138_2: pin names not known; wires that end beside it: X0, n3_to_8_decoder_74138_2_p2, X1, n3_to_8_decoder_74138_2_p4, X2, n3_to_8_decoder_74138_2_p6, n3_to_8_decoder_74138_2_p7, n3_to_8_decoder_74138_2_p8, n3_to_8_decoder_74138_2_p9, n3_to_8_decoder_74138_2_p10, n3_to_8_decoder_74138_2_p11, 1'b1, n3_to_8_decoder_74138_2_p13, n3_to_8_decoder_74138_2_p13
  not not_7 (n3_to_8_decoder_74138_2_p13, 1'b1);
  not not_8 (Y7, n3_to_8_decoder_74138_2_p11);
  not not_9 (Y6, n3_to_8_decoder_74138_2_p10);
  not not_10 (Y5, n3_to_8_decoder_74138_2_p9);
  not not_11 (Y4, n3_to_8_decoder_74138_2_p8);
  not not_12 (Y3, n3_to_8_decoder_74138_2_p7);
  not not_13 (Y2, n3_to_8_decoder_74138_2_p6);
  not not_14 (Y1, n3_to_8_decoder_74138_2_p4);
  not not_15 (Y0, n3_to_8_decoder_74138_2_p2);

  // Notes on the sheet:
  //   B0'
endmodule
